# Fritzing sketch TFT-Wiring (saved by Fritzing 0.9.4)
breadboards: 1

parts:
  U1 = NodeMCU V1.0
  LCD1 = TFT 1.8 inch 160x128 w SD
  Bauteil1 = Breadboard Power Supply Board SMD

nets:
  N1: U1.D3, LCD1.pin4
  N2: U1.D4, LCD1.pin_5
  GND: U1.GND, LCD1.pin2, Bauteil1.GND
  N3: U1.D5, LCD1.pin_7
  N4: U1.D7, LCD1.pin_6
  N5: U1.D8, LCD1.pin3
  N6: LCD1.pin_1, LCD1.pin_8, Bauteil1.VCC

notes:
  VCC: 5V
  VCC: 3.3V

custom parts:
  NodeMCU V1.0: ESP8266 based NodeMCU
  TFT 1.8 inch 160x128 w SD: This is a generic 1.8 tft spi lcd display available on ebay and others. The 1.8" display has 128x160 color pixels.
